// Logisim project 2012468642_Md Saiyem Raiyan_LAB 1.circ as structural Verilog: 8 circuits, main circuit main
module main (
  input  A,
  input  B,
  input  C,
  input  A_2,
  input  C_2,
  input  A_3,
  input  B_2,
  input  B_3,
  input  C_3,
  output out_10,
  output out_11,
  output F,
  output l1,
  output l2,
  output l3,
  output F_2
);

  wire and_1_out, and_2_out, and_3_out, n2_input_or_ic_7432_1_out_11, not_1_out, not_2_out, or_1_out;

  NOT_IC_7404 not_ic_7404_1 (
    .in_2(A), .in_3(B), .in_5(1'b0), .in_6(1'b1), .out_9(out_10), .out_10(out_11));  // open: in_4, in_7, out_11, out_12, out_13, out_14, VCC, GND
  _2_input_AND_IC_7408 u_2_input_and_ic_7408_1 (
    .VCC(out_10), .in_2(C), .in_3(A), .in_4(out_11), .in_5(1'b0), .in_6(1'b1), .in_9(C), .GND(B),
    .out_11(l1), .out_12(l3), .out_13(l2));  // open: in_7, in_8, out_14
  _2_input_or_IC_7432 u_2_input_or_ic_7432_1 (
    .VCC(l1), .in_2(n2_input_or_ic_7432_1_out_11), .in_3(A), .in_4(l3), .in_5(1'b0), .in_6(1'b1),
    .out_11(n2_input_or_ic_7432_1_out_11), .out_12(F_2));  // open: in_7, in_8, in_9, GND, out_13, out_14
  not not_1 (not_1_out, A_2);
  not not_2 (not_2_out, A_3);
  and and_1 (and_1_out, not_1_out, C_2);
  and and_2 (and_2_out, not_2_out, B_2);
  and and_3 (and_3_out, B_3, C_3);
  or or_1 (or_1_out, and_1_out, and_2_out);
  or or_2 (F, or_1_out, and_3_out);

  // Notes on the sheet:
  //                          ID: 2012468642
  //                      Md Saiyem Raiyan
  //   l1
  //   l2
  //   l3
endmodule

module _2_input_or_IC_7432 (
  input  VCC,
  input  in_2,
  input  in_3,
  input  in_4,
  input  in_5,
  input  in_6,
  input  in_7,
  input  in_8,
  input  in_9,
  input  GND,
  output out_11,
  output out_12,
  output out_13,
  output out_14
);

  or or_1 (out_11, in_2, in_3);
  or or_2 (out_12, in_4, in_5);
  or or_3 (out_13, in_6, in_7);
  or or_4 (out_14, in_8, in_9);
endmodule

module NOT_IC_7404 (
  input  VCC,
  input  in_2,
  input  in_3,
  input  in_4,
  input  in_5,
  input  in_6,
  input  in_7,
  input  GND,
  output out_9,
  output out_10,
  output out_11,
  output out_12,
  output out_13,
  output out_14
);

  not not_1 (out_9, in_2);
  not not_2 (out_10, in_3);
  not not_3 (out_11, in_4);
  not not_4 (out_12, in_5);
  not not_5 (out_13, in_6);
  not not_6 (out_14, in_7);
endmodule

module _2_input_NAND_IC_7400 (
  input  VCC,
  input  in_2,
  input  in_3,
  input  in_4,
  input  in_5,
  input  in_6,
  input  in_7,
  input  in_8,
  input  in_9,
  input  GND,
  output out_11,
  output out_12,
  output out_13,
  output out_14
);

  nand nand_1 (out_11, in_2, in_3);
  nand nand_2 (out_12, in_4, in_5);
  nand nand_3 (out_13, in_6, in_7);
  nand nand_4 (out_14, in_8, in_9);
endmodule

module _2_input_NOR_IC_7402 (
  input  VCC,
  input  in_2,
  input  in_3,
  input  in_4,
  input  in_5,
  input  in_6,
  input  in_7,
  input  in_8,
  input  in_9,
  input  GND,
  output out_11,
  output out_12,
  output out_13,
  output out_14
);

  nor nor_1 (out_11, in_2, in_3);
  nor nor_2 (out_12, in_4, in_5);
  nor nor_3 (out_13, in_6, in_7);
  nor nor_4 (out_14, in_8, in_9);
endmodule

module _2_input_XOR_IC_7486 (
  input  VCC,
  input  in_2,
  input  in_3,
  input  in_4,
  input  in_5,
  input  in_6,
  input  in_7,
  input  in_8,
  input  in_9,
  input  GND,
  output out_11,
  output out_12,
  output out_13,
  output out_14
);

  xor xor_1 (out_11, in_2, in_3);
  xor xor_2 (out_12, in_4, in_5);
  xor xor_3 (out_13, in_6, in_7);
  xor xor_4 (out_14, in_8, in_9);
endmodule

module _2_input_of_XNOR_74266 (
  input  VCC,
  input  in_2,
  input  in_3,
  input  in_4,
  input  in_5,
  input  in_6,
  input  in_7,
  input  in_8,
  input  in_9,
  input  GND,
  output out_11,
  output out_12,
  output out_13,
  output out_14
);

  xnor xnor_1 (out_11, in_2, in_3);
  xnor xnor_2 (out_12, in_4, in_5);
  xnor xnor_3 (out_13, in_6, in_7);
  xnor xnor_4 (out_14, in_8, in_9);
endmodule

module _2_input_AND_IC_7408 (
  input  VCC,
  input  in_2,
  input  in_3,
  input  in_4,
  input  in_5,
  input  in_6,
  input  in_7,
  input  in_8,
  input  in_9,
  input  GND,
  output out_11,
  output out_12,
  output out_13,
  output out_14
);

  and and_1 (out_11, in_2, in_3);
  and and_2 (out_12, in_4, in_5);
  and and_3 (out_13, in_6, in_7);
  and and_4 (out_14, in_8, in_9);
endmodule
