// Logisim project 2012468642_Md Saiyem Raiyan_LAB 4.circ as structural Verilog: 10 circuits, main circuit main
module main (
  input  W,
  input  X,
  input  Y,
  input  Z,
  output A,
  output B,
  output C,
  output A_2,
  output D,
  output B_2,
  output C_2,
  output D_2
);

  wire n2_input_and_ic_7408_1_out_11, n2_input_and_ic_7408_1_out_12, n2_input_and_ic_7408_1_out_13,
       n2_input_and_ic_7408_1_out_14, n2_input_and_ic_7408_2_out_11, n2_input_and_ic_7408_2_out_12,
       n3_input_and_ic_4073_1_f, not_1_out, not_2_out, not_3_out, not_5_out, not_6_out, not_7_out,
       X_prime_Y_out, X_prime_Z_out, XY_out, XY_prime_Z_out, XZ_out, Y_prime_Z_prime_out, YZ_out;

  not not_1 (not_1_out, W);
  not not_2 (not_2_out, X);
  not not_3 (not_3_out, Y);
  not not_4 (D, Z);
  and XZ (XZ_out, X, Z);
  and XY (XY_out, X, Y);
  and X_prime_Y (X_prime_Y_out, not_2_out, Z);
  and X_prime_Z (X_prime_Z_out, not_2_out, Y);
  and XY_prime_Z (XY_prime_Z_out, X, D, not_3_out);
  and Y_prime_Z_prime (Y_prime_Z_prime_out, not_3_out, D);
  and YZ (YZ_out, Y, Z);
  or or_1 (A, W, XZ_out, XY_out);
  or or_2 (B, X_prime_Y_out, X_prime_Z_out, XY_prime_Z_out);
  or or_3 (C, Y_prime_Z_prime_out, YZ_out);
  not not_5 (not_5_out, W);
  not not_6 (not_6_out, X);
  not not_7 (not_7_out, Y);
  not not_8 (D_2, Z);
  NOT_IC_7404 not_ic_7404_1 (
    .VCC(1'b1), .in_2(W), .in_3(X), .in_4(Y), .in_5(Z), .GND(1'b0), .out_9(not_5_out), .out_10(not_6_out),
    .out_11(not_7_out), .out_12(D_2));  // open: in_6, in_7, out_13, out_14
  _2_input_AND_IC_7408 u_2_input_and_ic_7408_1 (
    .VCC(1'b1), .in_2(X), .in_3(Y), .in_4(X), .in_5(Y), .in_6(Y), .in_7(not_6_out), .GND(1'b0),
    .out_11(n2_input_and_ic_7408_1_out_11), .out_12(n2_input_and_ic_7408_1_out_12),
    .out_13(n2_input_and_ic_7408_1_out_13), .in_8(not_6_out), .out_14(n2_input_and_ic_7408_1_out_14), .in_9(Z));
  _3_input_AND_IC_4073 u_3_input_and_ic_4073_1 (
    .VCC(1'b1), .A1(X), .B1(not_7_out), .C1(D_2), .GND(1'b0), .F(n3_input_and_ic_4073_1_f));  // open: A2, B2, C2, A3, B3, C3, F_2, F_3
  _2_input_AND_IC_7408 u_2_input_and_ic_7408_2 (
    .VCC(1'b1), .in_2(not_7_out), .in_3(D_2), .in_4(Y), .in_5(Z), .GND(1'b0),
    .out_11(n2_input_and_ic_7408_2_out_11), .out_12(n2_input_and_ic_7408_2_out_12));  // open: in_6, in_7, out_13, in_8, out_14, in_9
  _3_input_or_IC_4075 u_3_input_or_ic_4075_1 (
    .VCC(1'b1), .A1(n2_input_and_ic_7408_1_out_11), .B1(n2_input_and_ic_7408_1_out_12), .C1(W),
    .A2(n3_input_and_ic_4073_1_f), .B2(n2_input_and_ic_7408_1_out_14), .C2(n2_input_and_ic_7408_1_out_13),
    .A3(n2_input_and_ic_7408_2_out_11), .B3(n2_input_and_ic_7408_2_out_11),
    .C3(n2_input_and_ic_7408_2_out_12), .GND(1'b0), .F(A_2), .F_2(B_2), .F_3(C_2));

  // Notes on the sheet:
  //   Md Saiyem Raiyan
  //   ID: 2012468642
  //   Md Saiyem Raiyan
  //   ID: 2012468642
endmodule

module _2_input_AND_IC_7408 (
  input  VCC,
  input  in_2,
  input  in_3,
  input  in_4,
  input  in_5,
  input  in_6,
  input  in_7,
  input  in_8,
  input  in_9,
  input  GND,
  output out_11,
  output out_12,
  output out_13,
  output out_14
);

  and and_1 (out_11, in_2, in_3);
  and and_2 (out_12, in_4, in_5);
  and and_3 (out_13, in_6, in_7);
  and and_4 (out_14, in_8, in_9);
endmodule

module _2_input_OR_IC_7432 (
  input  VCC,
  input  in_2,
  input  in_3,
  input  in_4,
  input  in_5,
  input  in_6,
  input  in_7,
  input  in_8,
  input  in_9,
  input  GND,
  output out_11,
  output out_12,
  output out_13,
  output out_14
);

  or or_1 (out_11, in_2, in_3);
  or or_2 (out_12, in_4, in_5);
  or or_3 (out_13, in_6, in_7);
  or or_4 (out_14, in_8, in_9);
endmodule

module NOT_IC_7404 (
  input  VCC,
  input  in_2,
  input  in_3,
  input  in_4,
  input  in_5,
  input  in_6,
  input  in_7,
  input  GND,
  output out_9,
  output out_10,
  output out_11,
  output out_12,
  output out_13,
  output out_14
);

  not not_1 (out_9, in_2);
  not not_2 (out_10, in_3);
  not not_3 (out_11, in_4);
  not not_4 (out_12, in_5);
  not not_5 (out_13, in_6);
  not not_6 (out_14, in_7);
endmodule

module _2_input_NAND_IC_7400 (
  input  VCC,
  input  in_2,
  input  in_3,
  input  in_4,
  input  in_5,
  input  in_6,
  input  in_7,
  input  in_8,
  input  in_9,
  input  GND,
  output out_11,
  output out_12,
  output out_13,
  output out_14
);

  nand nand_1 (out_11, in_2, in_3);
  nand nand_2 (out_12, in_4, in_5);
  nand nand_3 (out_13, in_6, in_7);
  nand nand_4 (out_14, in_8, in_9);
endmodule

module _2_input_NOR_IC_7402 (
  input  VCC,
  input  in_2,
  input  in_3,
  input  in_4,
  input  in_5,
  input  in_6,
  input  in_7,
  input  in_8,
  input  in_9,
  input  GND,
  output out_11,
  output out_12,
  output out_13,
  output out_14
);

  nor nor_1 (out_11, in_2, in_3);
  nor nor_2 (out_12, in_4, in_5);
  nor nor_3 (out_13, in_6, in_7);
  nor nor_4 (out_14, in_8, in_9);
endmodule

module _2_input_XOR_IC_7486 (
  input  VCC,
  input  in_2,
  input  in_3,
  input  in_4,
  input  in_5,
  input  in_6,
  input  in_7,
  input  in_8,
  input  in_9,
  input  GND,
  output out_11,
  output out_12,
  output out_13,
  output out_14
);

  xor xor_1 (out_11, in_2, in_3);
  xor xor_2 (out_12, in_4, in_5);
  xor xor_3 (out_13, in_6, in_7);
  xor xor_4 (out_14, in_8, in_9);
endmodule

module _2_input_XNOR_74266 (
  input  VCC,
  input  in_2,
  input  in_3,
  input  in_4,
  input  in_5,
  input  in_6,
  input  in_7,
  input  in_8,
  input  in_9,
  input  GND,
  output out_11,
  output out_12,
  output out_13,
  output out_14
);

  xnor xnor_1 (out_11, in_2, in_3);
  xnor xnor_2 (out_12, in_4, in_5);
  xnor xnor_3 (out_13, in_6, in_7);
  xnor xnor_4 (out_14, in_8, in_9);
endmodule

module _3_input_AND_IC_4073 (
  input  VCC,
  input  A1,
  input  B1,
  input  C1,
  input  A2,
  input  B2,
  input  C2,
  input  A3,
  input  B3,
  input  C3,
  input  GND,
  output F,
  output F_2,
  output F_3
);

  and and_1 (F, A1, B1, C1);
  and and_2 (F_2, A2, B2, C2);
  and and_3 (F_3, A3, B3, C3);
endmodule

module _3_input_or_IC_4075 (
  input  VCC,
  input  A1,
  input  B1,
  input  C1,
  input  A2,
  input  B2,
  input  C2,
  input  A3,
  input  B3,
  input  C3,
  input  GND,
  output F,
  output F_2,
  output F_3
);

  or or_1 (F, A1, B1, C1);
  or or_2 (F_2, A2, B2, C2);
  or or_3 (F_3, A3, B3, C3);
endmodule
