// Logisim project Binary Arithmetic.circ as structural Verilog: 3 circuits
module _7486_XOR_IC (
  input  in_1,
  input  in_2,
  input  in_3,
  input  in_4,
  input  in_5,
  input  in_6,
  input  in_7,
  input  in_8,
  input  in_9,
  input  in_10,
  output out_11,
  output out_12,
  output out_13,
  output out_14
);

  xor xor_1 (out_11, in_2, in_3);
  xor xor_2 (out_12, in_4, in_5);
  xor xor_3 (out_13, in_6, in_7);
  xor xor_4 (out_14, in_8, in_9);
endmodule

module _7483_4_bit_Adder_IC (
  input  B4,
  input  B3,
  input  B2,
  input  B1,
  input  A4,
  input  A3,
  input  A2,
  input  A1,
  input  C_IN,
  input  VCC,
  input  GND,
  output C_OUT,
  output S4,
  output S3,
  output S2,
  output S1
);

  wire and_1_out, and_2_out, and_3_out, and_4_out, and_5_out, and_6_out, and_7_out, and_8_out, or_1_out,
       or_2_out, or_3_out, xor_1_out, xor_2_out, xor_3_out, xor_4_out;

  and and_1 (and_1_out, A1, B1);
  and and_2 (and_2_out, A2, B2);
  and and_3 (and_3_out, A3, B3);
  and and_4 (and_4_out, A4, B4);
  xor xor_1 (xor_1_out, A1, B1);
  xor xor_2 (xor_2_out, A2, B2);
  xor xor_3 (xor_3_out, A3, B3);
  xor xor_4 (xor_4_out, A4, B4);
  xor xor_5 (S1, xor_1_out, C_IN);
  and and_5 (and_5_out, xor_1_out, C_IN);
  xor xor_6 (S2, xor_2_out, or_1_out);
  and and_6 (and_6_out, xor_2_out, or_1_out);
  xor xor_7 (S3, xor_3_out, or_2_out);
  and and_7 (and_7_out, xor_3_out, or_2_out);
  xor xor_8 (S4, xor_4_out, or_3_out);
  and and_8 (and_8_out, xor_4_out, or_3_out);
  or or_1 (or_1_out, and_5_out, and_1_out);
  or or_2 (or_2_out, and_6_out, and_2_out);
  or or_3 (or_3_out, and_7_out, and_3_out);
  or or_4 (C_OUT, and_8_out, and_4_out);
endmodule

// C4
module circuit (
  input  [3:0] A,
  input  [3:0] B,
  input  Mode,
  input  [3:0] A_2,
  input  [3:0] B_2,
  input  Mode_2,
  output C4,
  output [3:0] S,
  output C4_2,
  output [3:0] S_2
);

  wire n7486_xor_ic_1_out_11, n7486_xor_ic_1_out_12, n7486_xor_ic_1_out_13, n7486_xor_ic_1_out_14, xor_1_out,
       xor_2_out, xor_3_out, xor_4_out;

  xor xor_1 (xor_1_out, B[0], Mode);
  xor xor_2 (xor_2_out, B[1], Mode);
  xor xor_3 (xor_3_out, B[2], Mode);
  xor xor_4 (xor_4_out, B[3], Mode);
  _7486_XOR_IC u_7486_xor_ic_1 (
    .in_1(1'b1), .in_2(B_2[0]), .in_3(Mode_2), .in_4(B_2[1]), .in_5(Mode_2), .in_6(B_2[2]), .in_7(Mode_2),
    .in_8(Mode_2), .in_9(B_2[3]), .in_10(1'b0), .out_11(n7486_xor_ic_1_out_11),
    .out_12(n7486_xor_ic_1_out_12), .out_13(n7486_xor_ic_1_out_13), .out_14(n7486_xor_ic_1_out_14));
  _7483_4_bit_Adder_IC u_7483_4_bit_adder_ic_1 (
    .B4(xor_4_out), .B3(xor_3_out), .B2(xor_2_out), .B1(xor_1_out), .A4(A[3]), .A3(A[2]), .A2(A[1]),
    .A1(A[0]), .C_IN(Mode), .VCC(1'b1), .GND(1'b0), .C_OUT(C4), .S4(S[3]), .S3(S[2]), .S2(S[1]), .S1(S[0]));
  _7483_4_bit_Adder_IC u_7483_4_bit_adder_ic_2 (
    .B4(n7486_xor_ic_1_out_14), .B3(n7486_xor_ic_1_out_13), .B2(n7486_xor_ic_1_out_12),
    .B1(n7486_xor_ic_1_out_11), .A4(A_2[3]), .A3(A_2[2]), .A2(A_2[1]), .A1(A_2[0]), .C_IN(Mode_2),
    .VCC(1'b1), .GND(1'b0), .C_OUT(C4_2), .S4(S_2[3]), .S3(S_2[2]), .S2(S_2[1]), .S1(S_2[0]));

  // Notes on the sheet:
  //   Md Saiyem Raiyan
  //   ID: 2012468642
  //   Md Saiyem Raiyan
  //   ID: 2012468642
endmodule
