// Logisim project Combinational Logic Design.circ as structural Verilog: 10 circuits, main circuit main
module main (
  input  A,
  input  B,
  input  C,
  output F,
  output F_2,
  output F_3,
  output out_7
);

  wire and_1_out, and_2_out, and_3_out, and_4_out, n3_input_and_ic_4073_1_f, n3_input_and_ic_4073_1_f_2,
       n3_input_and_ic_4073_1_f_3, n3_input_and_ic_4073_2_f_2, n3_input_or_ic_4075_2_f,
       n3_input_or_ic_4075_2_f_2, n3_input_or_ic_4075_3_f, n3_input_or_ic_4075_3_f_2,
       n3_input_or_ic_4075_3_f_3, not_1_out, not_2_out, not_3_out, not_4_out, not_5_out, not_6_out,
       not_ic_7404_1_out_9, not_ic_7404_1_out_10, not_ic_7404_1_out_11, not_ic_7404_2_out_9,
       not_ic_7404_2_out_10, not_ic_7404_2_out_11, or_2_out, or_3_out, or_4_out, or_5_out, or_6_out;

  not not_1 (not_1_out, B);
  not not_2 (not_2_out, A);
  not not_3 (not_3_out, C);
  and and_1 (and_1_out, not_2_out, not_1_out, C);
  and and_2 (and_2_out, not_2_out, B, not_3_out);
  and and_3 (and_3_out, A, B, not_3_out);
  NOT_IC_7404 not_ic_7404_1 (
    .VCC(1'b1), .in_2(A), .in_3(B), .in_4(C), .GND(1'b0), .out_9(not_ic_7404_1_out_9),
    .out_10(not_ic_7404_1_out_10), .out_11(not_ic_7404_1_out_11));  // open: in_5, in_6, in_7, out_12, out_13, out_14
  _3_input_AND_IC_4073 u_3_input_and_ic_4073_1 (
    .VCC(1'b1), .A1(not_ic_7404_1_out_9), .B1(B), .C1(not_ic_7404_1_out_11), .A2(not_ic_7404_1_out_10),
    .B2(not_ic_7404_1_out_9), .C2(C), .A3(A), .B3(B), .C3(not_ic_7404_1_out_11),
    .F(n3_input_and_ic_4073_1_f), .F_2(n3_input_and_ic_4073_1_f_2), .F_3(n3_input_and_ic_4073_1_f_3));  // open: GND
  or or_1 (F, and_1_out, and_2_out, and_3_out);
  _3_input_or_IC_4075 u_3_input_or_ic_4075_1 (
    .VCC(1'b1), .A1(n3_input_and_ic_4073_1_f), .B1(n3_input_and_ic_4073_1_f_3),
    .C1(n3_input_and_ic_4073_1_f_2), .GND(1'b0), .F(out_7));  // open: A2, B2, C2, A3, B3, C3, F_2, F_3
  not not_4 (not_4_out, A);
  not not_5 (not_5_out, B);
  not not_6 (not_6_out, C);
  or or_2 (or_2_out, A, B, C);
  or or_3 (or_3_out, A, not_5_out, not_6_out);
  or or_4 (or_4_out, not_4_out, B, C);
  or or_5 (or_5_out, not_4_out, B, not_6_out);
  or or_6 (or_6_out, not_4_out, not_5_out, not_6_out);
  _3_input_or_IC_4075 u_3_input_or_ic_4075_2 (
    .VCC(1'b1), .A1(A), .B1(not_ic_7404_2_out_9), .C1(not_ic_7404_2_out_10), .A2(A), .B2(B), .C2(C),
    .GND(1'b0), .F(n3_input_or_ic_4075_2_f), .F_2(n3_input_or_ic_4075_2_f_2));  // open: A3, B3, C3, F_3
  NOT_IC_7404 not_ic_7404_2 (
    .VCC(1'b1), .in_2(B), .in_3(C), .in_4(A), .GND(1'b0), .out_9(not_ic_7404_2_out_9),
    .out_10(not_ic_7404_2_out_10), .out_11(not_ic_7404_2_out_11));  // open: in_5, in_6, in_7, out_12, out_13, out_14
  _3_input_or_IC_4075 u_3_input_or_ic_4075_3 (
    .A1(not_ic_7404_2_out_11), .B1(not_ic_7404_2_out_10), .C1(B), .A2(not_ic_7404_2_out_11), .B2(B), .C2(C),
    .A3(not_ic_7404_2_out_11), .B3(not_ic_7404_2_out_10), .C3(not_ic_7404_2_out_9), .GND(1'b0),
    .F(n3_input_or_ic_4075_3_f), .F_2(n3_input_or_ic_4075_3_f_2), .F_3(n3_input_or_ic_4075_3_f_3));  // open: VCC
  and and_4 (and_4_out, or_2_out, or_3_out, or_4_out);
  and and_5 (F_2, and_4_out, or_5_out, or_6_out);
  _3_input_AND_IC_4073 u_3_input_and_ic_4073_2 (
    .VCC(1'b1), .A2(n3_input_or_ic_4075_2_f_2), .B2(n3_input_or_ic_4075_2_f), .C2(n3_input_or_ic_4075_3_f_3),
    .A3(n3_input_and_ic_4073_2_f_2), .B3(n3_input_or_ic_4075_3_f), .C3(n3_input_or_ic_4075_3_f_2),
    .GND(1'b0), .F_2(n3_input_and_ic_4073_2_f_2), .F_3(F_3));  // open: A1, B1, C1, F

  // Notes on the sheet:
  //   Name: Md Saiyem Raiyan
  //   ID: 2012468642
  //   A
  //   B
  //   C
  //   ID: 2012468642
  //   Name: Md Saiyem Raiyan
endmodule

module _2_input_AND_IC_7408 (
  input  VCC,
  input  in_2,
  input  in_3,
  input  in_4,
  input  in_5,
  input  in_6,
  input  in_7,
  input  in_8,
  input  in_9,
  input  GND,
  output out_11,
  output out_12,
  output out_13,
  output out_14
);

  and and_1 (out_11, in_2, in_3);
  and and_2 (out_12, in_4, in_5);
  and and_3 (out_13, in_6, in_7);
  and and_4 (out_14, in_8, in_9);
endmodule

module _2_input_OR_IC_7432 (
  input  VCC,
  input  in_2,
  input  in_3,
  input  in_4,
  input  in_5,
  input  in_6,
  input  in_7,
  input  in_8,
  input  in_9,
  input  GND,
  output out_11,
  output out_12,
  output out_13,
  output out_14
);

  or or_1 (out_11, in_2, in_3);
  or or_2 (out_12, in_4, in_5);
  or or_3 (out_13, in_6, in_7);
  or or_4 (out_14, in_8, in_9);
endmodule

module NOT_IC_7404 (
  input  VCC,
  input  in_2,
  input  in_3,
  input  in_4,
  input  in_5,
  input  in_6,
  input  in_7,
  input  GND,
  output out_9,
  output out_10,
  output out_11,
  output out_12,
  output out_13,
  output out_14
);

  not not_1 (out_9, in_2);
  not not_2 (out_10, in_3);
  not not_3 (out_11, in_4);
  not not_4 (out_12, in_5);
  not not_5 (out_13, in_6);
  not not_6 (out_14, in_7);
endmodule

module _2_input_NAND_IC_7400 (
  input  VCC,
  input  in_2,
  input  in_3,
  input  in_4,
  input  in_5,
  input  in_6,
  input  in_7,
  input  in_8,
  input  in_9,
  input  GND,
  output out_11,
  output out_12,
  output out_13,
  output out_14
);

  nand nand_1 (out_11, in_2, in_3);
  nand nand_2 (out_12, in_4, in_5);
  nand nand_3 (out_13, in_6, in_7);
  nand nand_4 (out_14, in_8, in_9);
endmodule

module _2_input_NOR_IC_7402 (
  input  VCC,
  input  in_2,
  input  in_3,
  input  in_4,
  input  in_5,
  input  in_6,
  input  in_7,
  input  in_8,
  input  in_9,
  input  GND,
  output out_11,
  output out_12,
  output out_13,
  output out_14
);

  nor nor_1 (out_11, in_2, in_3);
  nor nor_2 (out_12, in_4, in_5);
  nor nor_3 (out_13, in_6, in_7);
  nor nor_4 (out_14, in_8, in_9);
endmodule

module _2_input_XOR_IC_7486 (
  input  VCC,
  input  in_2,
  input  in_3,
  input  in_4,
  input  in_5,
  input  in_6,
  input  in_7,
  input  in_8,
  input  in_9,
  input  GND,
  output out_11,
  output out_12,
  output out_13,
  output out_14
);

  xor xor_1 (out_11, in_2, in_3);
  xor xor_2 (out_12, in_4, in_5);
  xor xor_3 (out_13, in_6, in_7);
  xor xor_4 (out_14, in_8, in_9);
endmodule

module _2_input_XNOR_74266 (
  input  VCC,
  input  in_2,
  input  in_3,
  input  in_4,
  input  in_5,
  input  in_6,
  input  in_7,
  input  in_8,
  input  in_9,
  input  GND,
  output out_11,
  output out_12,
  output out_13,
  output out_14
);

  xnor xnor_1 (out_11, in_2, in_3);
  xnor xnor_2 (out_12, in_4, in_5);
  xnor xnor_3 (out_13, in_6, in_7);
  xnor xnor_4 (out_14, in_8, in_9);
endmodule

module _3_input_AND_IC_4073 (
  input  VCC,
  input  A1,
  input  B1,
  input  C1,
  input  A2,
  input  B2,
  input  C2,
  input  A3,
  input  B3,
  input  C3,
  input  GND,
  output F,
  output F_2,
  output F_3
);

  and and_1 (F, A1, B1, C1);
  and and_2 (F_2, A2, B2, C2);
  and and_3 (F_3, A3, B3, C3);
endmodule

module _3_input_or_IC_4075 (
  input  VCC,
  input  A1,
  input  B1,
  input  C1,
  input  A2,
  input  B2,
  input  C2,
  input  A3,
  input  B3,
  input  C3,
  input  GND,
  output F,
  output F_2,
  output F_3
);

  or or_1 (F, A1, B1, C1);
  or or_2 (F_2, A2, B2, C2);
  or or_3 (F_3, A3, B3, C3);
endmodule
