// Logisim project Flip-Flops and Shift Registers.circ as structural Verilog: 1 circuit, main circuit main
module main (
  input  K,
  input  J,
  input  J_2,
  input  K_2,
  input  T,
  input  T_2,
  input  T_3,
  input  D,
  input  D_2,
  input  D_3,
  input  in_11,
  input  in_12,
  input  in_13,
  output Q,
  output out_15,
  output Q_prime,
  output out_17,
  output Q_2,
  output Q_prime_2,
  output out_20,
  output out_21,
  output out_22,
  output out_23,
  output out_24,
  output out_25,
  output out_26,
  output out_27,
  output out_28,
  output out_29,
  output out_30
);

  wire and_1_out, and_2_out, and_3_out, and_4_out, and_5_out, and_6_out, clock_1_out, clock_2_out,
       clock_3_out, clock_4_out, clock_5_out, clock_6_out, clock_7_out, clock_8_out, clock_9_out, d_ff_1_q,
       d_ff_2_q, d_ff_3_q, not_1_out, not_2_out;

  Clock clock_1 (.out(clock_1_out));
  Clock clock_2 (.out(clock_2_out));
  Clock clock_3 (.out(clock_3_out));
  not not_1 (not_1_out, D);
  and and_1 (and_1_out, out_24, D, clock_3_out);
  and and_2 (and_2_out, clock_3_out, not_1_out, out_25);
  and and_3 (and_3_out, Q, K, clock_1_out);
  and and_4 (and_4_out, clock_1_out, J_2, Q_prime);
  and and_5 (and_5_out, Q_2, T, clock_2_out);
  and and_6 (and_6_out, clock_2_out, T, Q_prime_2);
  nor nor_1 (out_24, and_1_out, out_25);
  nor nor_2 (out_25, out_24, and_2_out);
  Clock clock_4 (.out(clock_4_out));
  nor nor_3 (Q, and_3_out, Q_prime);
  nor nor_4 (Q_prime, Q, and_4_out);
  nor nor_5 (Q_2, and_5_out, Q_prime_2);
  nor nor_6 (Q_prime_2, Q_2, and_6_out);
  D_Flip_Flop d_ff_1 (.clk(clock_4_out), .D(in_11), .Q(d_ff_1_q), .preset(in_12), .reset(in_13));  // open: Qn, en
  D_Flip_Flop d_ff_2 (.clk(clock_4_out), .D(d_ff_1_q), .Q(d_ff_2_q), .preset(in_12), .reset(in_13));  // open: Qn, en
  D_Flip_Flop d_ff_3 (.clk(clock_4_out), .D(d_ff_2_q), .Q(d_ff_3_q), .preset(in_12), .reset(in_13));  // open: Qn, en
  Clock clock_5 (.out(clock_5_out));
  Clock clock_6 (.out(clock_6_out));
  Clock clock_7 (.out(clock_7_out));
  D_Flip_Flop d_ff_4 (.clk(clock_4_out), .D(d_ff_3_q), .Qn(out_30), .preset(in_12), .reset(in_13));  // open: Q, en
  J_K_Flip_Flop j_k_ff_1 (.J(J), .clk(clock_5_out), .K(K_2), .Q(out_15), .Qn(out_17));  // open: preset, en, reset
  T_Flip_Flop t_ff_1 (.clk(clock_6_out), .T(T_3), .Q(out_20), .Qn(out_22));  // open: preset, reset, en
  D_Flip_Flop d_ff_5 (.clk(clock_7_out), .D(D_3), .Q(out_26), .Qn(out_28));  // open: preset, en, reset
  Clock clock_8 (.out(clock_8_out));
  Clock clock_9 (.out(clock_9_out));
  not not_2 (not_2_out, D_2);
  J_K_Flip_Flop j_k_ff_2 (.J(T_2), .clk(clock_8_out), .K(T_2), .Q(out_21), .Qn(out_23));  // open: preset, en, reset
  J_K_Flip_Flop j_k_ff_3 (
    .J(D_2), .clk(clock_9_out), .K(not_2_out), .Q(out_27), .Qn(out_29));  // open: preset, en, reset

  // Notes on the sheet:
  //   T Flip Flop using gates
  //   JK Flip Flop using gates
  //   D Flip Flop using gates
  //   Right Shift Register
  //   JK Flip Flop
  //   T Flip Flop
  //   D Flip Flop 
  //   T Flip Flop using JK Flip Flop
  //   D Flip Flop using JK Flip Flop
endmodule
