// Logisim project MUX and Decoder.circ as structural Verilog: 5 circuits, main circuit main
module main (
  input  [2:0] S,
  input  [3:0] S_2,
  input  [2:0] S_3,
  output out_4,
  output out_5,
  output out_6,
  output out_7,
  output out_8,
  output out_9,
  output out_10,
  output out_11,
  output out_12,
  output out_13
);

  wire decoder_1_out0, decoder_1_out1, decoder_1_out2, decoder_1_out3, decoder_1_out4, decoder_1_out5,
       decoder_1_out6, decoder_1_out7;

  _4_1_MUX u_4_1_mux_1 (.I0(1'b1), .I1(1'b0), .I2(S[0]), .I3(S[0]), .S1(S[2]), .S0(S[1]), .Output(out_5));
  Decoder #(.select(3)) decoder_1 (
    .out0(decoder_1_out0), .out1(decoder_1_out1), .out2(decoder_1_out2), .out3(decoder_1_out3),
    .out4(decoder_1_out4), .out5(decoder_1_out5), .out6(decoder_1_out6), .out7(decoder_1_out7), .sel(S_3));  // open: en
  not not_1 (out_6, decoder_1_out0);
  not not_2 (out_7, decoder_1_out1);
  not not_3 (out_8, decoder_1_out2);
  not not_4 (out_9, decoder_1_out3);
  not not_5 (out_10, decoder_1_out4);
  not not_6 (out_11, decoder_1_out5);
  not not_7 (out_12, decoder_1_out6);
  not not_8 (out_13, decoder_1_out7);
  Multiplexer #(.select(3)) multiplexer_1 (
    .in0(1'b1), .in1(S_2[0]), .in2(S_2[0]), .in3(1'b0), .in4(1'b1), .in5(1'b0), .in6(1'b0), .in7(1'b1),
    .out(out_4), .sel(S_2[3:1]));  // open: en

  // Notes on the sheet:
  //   ABC
  //   Experiment 1
  //   CBA
  //   Experiment 3
  //   ABCD
  //   Experiment 2
  //   ID: 2012468642
  //   Name: Md Saiyem Raiyan
endmodule

module _2_input_And_Ic_7408 (
  input  Vcc,
  input  in_2,
  input  in_3,
  input  in_4,
  input  in_5,
  input  in_6,
  input  in_7,
  input  in_8,
  input  in_9,
  input  GND,
  output out_11,
  output out_12,
  output out_13,
  output out_14
);

  and and_1 (out_11, in_2, in_3);
  and and_2 (out_12, in_4, in_5);
  and and_3 (out_13, in_6, in_7);
  and and_4 (out_14, in_8, in_9);
endmodule

module _2_Input_Or_Ic__7432 (
  input  Vcc,
  input  in_2,
  input  in_3,
  input  in_4,
  input  in_5,
  input  in_6,
  input  in_7,
  input  in_8,
  input  in_9,
  input  GND,
  output out_11,
  output out_12,
  output out_13,
  output out_14
);

  or or_1 (out_11, in_2, in_3);
  or or_2 (out_12, in_4, in_5);
  or or_3 (out_13, in_6, in_7);
  or or_4 (out_14, in_8, in_9);
endmodule

module NOT_IC_7404 (
  input  Vcc,
  input  in_2,
  input  in_3,
  input  in_4,
  input  in_5,
  input  in_6,
  input  in_7,
  input  GND,
  output out_9,
  output out_10,
  output out_11,
  output out_12,
  output out_13,
  output out_14
);

  not not_1 (out_9, in_2);
  not not_2 (out_10, in_3);
  not not_3 (out_11, in_4);
  not not_4 (out_12, in_5);
  not not_5 (out_13, in_6);
  not not_6 (out_14, in_7);
endmodule

module _4_1_MUX (
  input  I0,
  input  I1,
  input  I2,
  input  I3,
  input  S1,
  input  S0,
  output Output
);

  wire and_1_out, and_2_out, and_3_out, and_4_out, not_1_out, not_2_out, or_1_out, or_2_out;

  not not_1 (not_1_out, S1);
  not not_2 (not_2_out, S0);
  and and_1 (and_1_out, I0, not_1_out, not_2_out);
  and and_2 (and_2_out, I1, not_1_out, S0);
  and and_3 (and_3_out, I2, S1, not_2_out);
  and and_4 (and_4_out, I3, S1, S0);
  or or_1 (or_1_out, and_1_out, and_2_out);
  or or_2 (or_2_out, and_3_out, and_4_out);
  or or_3 (Output, or_1_out, or_2_out);
endmodule
