// Logisim project Seven Segment Display.circ as structural Verilog: 1 circuit, main circuit main
module main (
  input  D,
  input  C,
  input  B,
  input  A
);

  wire A_prime_B_2_out, A_prime_B_out, A_prime_B_prime_D_prime_out, A_prime_B_prime_out, A_prime_BC_out,
       A_prime_C_out, A_prime_C_prime_2_out, A_prime_C_prime_D_prime_out, A_prime_C_prime_out,
       AB_prime_C_out, AB_prime_D_out, AB_prime_out, ABC_prime_out, ABD_prime_out, AC_out, AD_prime_out,
       B_prime_C_out, B_prime_CD_prime_out, B_prime_D_out, B_prime_D_prime_out, BC_prime_out, BD_2_out,
       BD_out, C_prime_D_2_out, C_prime_D_out, CD_out, CD_prime_out, not_1_out, not_2_out, not_3_out,
       not_4_out, or_1_out, or_2_out, or_3_out, or_4_out, or_5_out, or_6_out, or_7_out;

  not not_1 (not_1_out, C);
  not not_2 (not_2_out, D);
  not not_3 (not_3_out, B);
  not not_4 (not_4_out, A);
  and AC (AC_out, A, C);
  and A_prime_C_prime (A_prime_C_prime_out, not_4_out, not_1_out);
  and A_prime_B_prime_D_prime (A_prime_B_prime_D_prime_out, not_4_out, not_3_out, not_2_out);
  and AB_prime_D (AB_prime_D_out, A, not_3_out, D);
  and ABD_prime (ABD_prime_out, A, B, not_2_out);
  and C_prime_D (C_prime_D_out, not_1_out, D);
  and CD_prime (CD_prime_out, C, not_2_out);
  and AB_prime (AB_prime_out, A, not_3_out);
  and AD_prime (AD_prime_out, not_2_out, A);
  and B_prime_D_prime (B_prime_D_prime_out, not_2_out, not_3_out);
  and B_prime_D (B_prime_D_out, not_3_out, D);
  and ABC_prime (ABC_prime_out, A, B, not_1_out);
  and AB_prime_C (AB_prime_C_out, A, not_3_out, C);
  and A_prime_C_prime_D_prime (A_prime_C_prime_D_prime_out, not_4_out, not_1_out, not_2_out);
  and A_prime_BC (A_prime_BC_out, not_4_out, B, C);
  and A_prime_B (A_prime_B_out, not_4_out, B);
  and CD (CD_out, C, D);
  and A_prime_C_prime_2 (A_prime_C_prime_2_out, not_4_out, not_1_out);
  and BD (BD_out, B, D);
  and A_prime_B_prime (A_prime_B_prime_out, not_4_out, not_3_out);
  and B_prime_C (B_prime_C_out, not_3_out, C);
  and A_prime_C (A_prime_C_out, not_4_out, C);
  and C_prime_D_2 (C_prime_D_2_out, not_1_out, D);
  and A_prime_B_2 (A_prime_B_2_out, not_4_out, B);
  and BD_2 (BD_2_out, B, D);
  and BC_prime (BC_prime_out, B, not_1_out);
  and B_prime_CD_prime (B_prime_CD_prime_out, not_3_out, C, not_2_out);
  or or_1 (or_1_out, B, D, AC_out, A_prime_C_prime_out);
  or or_2 (or_2_out, not_1_out, A_prime_B_prime_D_prime_out, AB_prime_D_out, ABD_prime_out);
  or or_3 (or_3_out, C_prime_D_out, CD_prime_out, AB_prime_out, AD_prime_out, B_prime_D_prime_out);
  or or_4 (or_4_out, B_prime_D_out, ABC_prime_out, AB_prime_C_out, A_prime_C_prime_D_prime_out, A_prime_BC_out);
  or or_5 (or_5_out, A_prime_B_out, CD_out, A_prime_C_prime_2_out, BD_out);
  or or_6 (or_6_out, D, A_prime_B_prime_out, B_prime_C_out, A_prime_C_out);
  or or_7 (or_7_out, C_prime_D_2_out, A_prime_B_2_out, BD_2_out, BC_prime_out, B_prime_CD_prime_out);
  _7_Segment_Display u_7_segment_display_1 (
    .g(or_7_out), .f(or_6_out), .a(or_1_out), .b(or_2_out), .e(or_5_out), .d(or_4_out), .c(or_3_out));  // open: dp

  // Notes on the sheet:
  //   Seven Segment Display
  //   c
  //   d
  //   e
  //   f
  //   g
  //   a
  //   b
  //   Md Saiyem Raiyan
  //   ID: 2012468642
endmodule
