// Logisim project Synchronous Sequential Circuits.circ as structural Verilog: 4 circuits, main circuit main
module main (
  input  X,
  input  X_2,
  input  X_3,
  output [1:0] out_4,
  output out_5,
  output [1:0] out_6,
  output [1:0] out_7,
  output out_8,
  output out_9
);

  wire A_qn, and_1_out, and_2_out, and_3_out, and_4_out, and_7_out, and_8_out, and_9_out, clock_1_out,
       clock_2_out, clock_3_out, DA_qn, not_1_out, not_2_out, not_3_out, or_1_out, or_2_out, TA_qn, TB_qn;

  not not_1 (not_1_out, X_2);
  Clock clock_1 (.out(clock_1_out));
  and and_1 (and_1_out, TA_qn, not_1_out);
  and and_2 (and_2_out, out_6[0], X_2);
  Clock clock_2 (.out(clock_2_out));
  or or_1 (or_1_out, and_3_out, and_2_out);
  and and_3 (and_3_out, and_1_out, TB_qn);
  not not_2 (not_2_out, X);
  and and_4 (and_4_out, A_qn, not_2_out);
  J_K_Flip_Flop TA (.J(X_2), .clk(clock_1_out), .K(X_2), .Q(out_6[1]), .Qn(TA_qn));  // open: preset, en, reset
  J_K_Flip_Flop TB (
    .J(or_1_out), .clk(clock_1_out), .K(or_1_out), .Q(out_6[0]), .Qn(TB_qn));  // open: preset, en, reset
  J_K_Flip_Flop A (.J(X), .clk(clock_2_out), .K(X), .Q(out_4[1]), .Qn(A_qn));  // open: preset, en, reset
  J_K_Flip_Flop B (.J(and_4_out), .clk(clock_2_out), .K(X), .Q(out_4[0]));  // open: Qn, preset, en, reset
  and and_5 (out_8, TA_qn, X_2);
  and and_6 (out_5, A_qn, X);
  Clock clock_3 (.out(clock_3_out));
  not not_3 (not_3_out, X_3);
  and and_7 (and_7_out, out_7[1], not_3_out);
  or or_2 (or_2_out, and_7_out, and_8_out);
  and and_8 (and_8_out, X_3, DA_qn);
  and and_9 (and_9_out, out_7[0], X_3);
  D_Flip_Flop DA (.clk(clock_3_out), .D(or_2_out), .Q(out_7[1]), .Qn(DA_qn));  // open: preset, en, reset
  D_Flip_Flop DB (.clk(clock_3_out), .D(and_9_out), .Q(out_7[0]));  // open: Qn, preset, en, reset
  and and_10 (out_9, DA_qn, X_3);

  // Notes on the sheet:
  //   Experiment 2: T using JK flip-flop
  //   Experiment 1: JK flip-flop
  //   Name: Md Saiyem Raiyan
  //   ID: 2012468642
  //   Experiment 3: D using JK flip-flop
endmodule

module _2_input_AND_IC_7408 (
  input  vcc,
  input  in_2,
  input  in_3,
  input  in_4,
  input  in_5,
  input  in_6,
  input  in_7,
  input  in_8,
  input  in_9,
  input  GND,
  output out_11,
  output out_12,
  output out_13,
  output out_14
);

  and and_1 (out_11, in_2, in_3);
  and and_2 (out_12, in_4, in_5);
  and and_3 (out_13, in_6, in_7);
  and and_4 (out_14, in_8, in_9);
endmodule

module _2_input_OR_IC_7432 (
  input  vcc,
  input  in_2,
  input  in_3,
  input  in_4,
  input  in_5,
  input  in_6,
  input  in_7,
  input  in_8,
  input  in_9,
  input  GND,
  output out_11,
  output out_12,
  output out_13,
  output out_14
);

  or or_1 (out_11, in_2, in_3);
  or or_2 (out_12, in_4, in_5);
  or or_3 (out_13, in_6, in_7);
  or or_4 (out_14, in_8, in_9);
endmodule

module NOT_IC_7404 (
  input  vcc,
  input  in_2,
  input  in_3,
  input  in_4,
  input  in_5,
  input  in_6,
  input  in_7,
  input  GND,
  output out_9,
  output out_10,
  output out_11,
  output out_12,
  output out_13,
  output out_14
);

  not not_1 (out_9, in_2);
  not not_2 (out_10, in_3);
  not not_3 (out_11, in_4);
  not not_4 (out_12, in_5);
  not not_5 (out_13, in_6);
  not not_6 (out_14, in_7);
endmodule
