// Logisim project Universal Logic gates.circ as structural Verilog: 8 circuits, main circuit main
module main (
  input  A,
  input  B,
  input  C,
  output F,
  output F_2,
  output F_3
);

  wire n2_input_nand_ic_7400_1_out_11, n2_input_nand_ic_7400_1_out_12, n2_input_nand_ic_7400_1_out_13,
       nand_1_out, nand_2_out, nand_3_out, nand_4_out, nand_5_out, nand_6_out, nand_7_out, nand_8_out,
       nand_9_out, nand_10_out;

  nand nand_1 (nand_1_out, C, C);
  nand nand_2 (nand_2_out, A, C);
  nand nand_3 (nand_3_out, B, nand_1_out);
  nand nand_4 (nand_4_out, C, C);
  _2_input_NAND_IC_7400 u_2_input_nand_ic_7400_1 (
    .VCC(C), .in_2(C), .in_3(n2_input_nand_ic_7400_1_out_11), .in_4(B), .in_5(1'b0), .in_6(1'b1), .in_7(A),
    .in_8(C), .in_9(n2_input_nand_ic_7400_1_out_13), .GND(n2_input_nand_ic_7400_1_out_12),
    .out_11(n2_input_nand_ic_7400_1_out_11), .out_12(n2_input_nand_ic_7400_1_out_12),
    .out_13(n2_input_nand_ic_7400_1_out_13), .out_14(F_3));
  nand nand_5 (nand_5_out, nand_3_out, nand_3_out);
  nand nand_6 (nand_6_out, A, C);
  nand nand_7 (nand_7_out, B, nand_4_out);
  nand nand_8 (nand_8_out, nand_2_out, nand_2_out);
  nand nand_9 (nand_9_out, nand_8_out, nand_8_out);
  nand nand_10 (nand_10_out, nand_5_out, nand_5_out);
  nand nand_11 (F, nand_9_out, nand_10_out);
  nand nand_12 (F_2, nand_6_out, nand_7_out);

  // Notes on the sheet:
  //                                 ID: 2012468642
  //   Md Saiyem Raiyan
endmodule

module _2_input_or_IC_7432 (
  input  VCC,
  input  in_2,
  input  in_3,
  input  in_4,
  input  in_5,
  input  in_6,
  input  in_7,
  input  in_8,
  input  in_9,
  input  GND,
  output out_11,
  output out_12,
  output out_13,
  output out_14
);

  or or_1 (out_11, in_2, in_3);
  or or_2 (out_12, in_4, in_5);
  or or_3 (out_13, in_6, in_7);
  or or_4 (out_14, in_8, in_9);
endmodule

module NOT_IC_7404 (
  input  VCC,
  input  in_2,
  input  in_3,
  input  in_4,
  input  in_5,
  input  in_6,
  input  in_7,
  input  GND,
  output out_9,
  output out_10,
  output out_11,
  output out_12,
  output out_13,
  output out_14
);

  not not_1 (out_9, in_2);
  not not_2 (out_10, in_3);
  not not_3 (out_11, in_4);
  not not_4 (out_12, in_5);
  not not_5 (out_13, in_6);
  not not_6 (out_14, in_7);
endmodule

module _2_input_NOR_IC_7402 (
  input  VCC,
  input  in_2,
  input  in_3,
  input  in_4,
  input  in_5,
  input  in_6,
  input  in_7,
  input  in_8,
  input  in_9,
  input  GND,
  output out_11,
  output out_12,
  output out_13,
  output out_14
);

  nor nor_1 (out_11, in_2, in_3);
  nor nor_2 (out_12, in_4, in_5);
  nor nor_3 (out_13, in_6, in_7);
  nor nor_4 (out_14, in_8, in_9);
endmodule

module _2_input_XOR_IC_7486 (
  input  VCC,
  input  in_2,
  input  in_3,
  input  in_4,
  input  in_5,
  input  in_6,
  input  in_7,
  input  in_8,
  input  in_9,
  input  GND,
  output out_11,
  output out_12,
  output out_13,
  output out_14
);

  xor xor_1 (out_11, in_2, in_3);
  xor xor_2 (out_12, in_4, in_5);
  xor xor_3 (out_13, in_6, in_7);
  xor xor_4 (out_14, in_8, in_9);
endmodule

module _2_input_of_XNOR_74266 (
  input  VCC,
  input  in_2,
  input  in_3,
  input  in_4,
  input  in_5,
  input  in_6,
  input  in_7,
  input  in_8,
  input  in_9,
  input  GND,
  output out_11,
  output out_12,
  output out_13,
  output out_14
);

  xnor xnor_1 (out_11, in_2, in_3);
  xnor xnor_2 (out_12, in_4, in_5);
  xnor xnor_3 (out_13, in_6, in_7);
  xnor xnor_4 (out_14, in_8, in_9);
endmodule

module _2_input_AND_IC_7408 (
  input  VCC,
  input  in_2,
  input  in_3,
  input  in_4,
  input  in_5,
  input  in_6,
  input  in_7,
  input  in_8,
  input  in_9,
  input  GND,
  output out_11,
  output out_12,
  output out_13,
  output out_14
);

  and and_1 (out_11, in_2, in_3);
  and and_2 (out_12, in_4, in_5);
  and and_3 (out_13, in_6, in_7);
  and and_4 (out_14, in_8, in_9);
endmodule

module _2_input_NAND_IC_7400 (
  input  VCC,
  input  in_2,
  input  in_3,
  input  in_4,
  input  in_5,
  input  in_6,
  input  in_7,
  input  in_8,
  input  in_9,
  input  GND,
  output out_11,
  output out_12,
  output out_13,
  output out_14
);

  nand nand_1 (out_11, in_2, in_3);
  nand nand_2 (out_12, in_4, in_5);
  nand nand_3 (out_13, in_6, in_7);
  nand nand_4 (out_14, in_8, in_9);
endmodule
